# Fritzing sketch Sketch (saved by Fritzing 0.9.3b)
breadboards: 1

parts:
  부품1 = Arduino Uno (Rev3)
  LED1 = 7-SEGMENT-4DIGIT-YOUNGSUN [package=7-segment-4digit-youngsun-longpads]
  R1 = Resistor [tolerance=±5% resistance=220 package=THT]
  R2 = Resistor [tolerance=±5% resistance=220 package=THT]
  R3 = Resistor [tolerance=±5% resistance=220 package=THT]
  R4 = Resistor [tolerance=±5% resistance=220 package=THT]

nets:
  N1: 부품1.D8, LED1.DIG2
  N2: 부품1.D9_PWM, LED1.C
  N3: 부품1.D10_PWM/SS, LED1.DIG3
  N4: 부품1.D11_PWM/MOSI, LED1.COL-A
  N5: 부품1.D0/RX, R1.Pin_1
  N6: 부품1.D1/TX, R2.Pin_1
  N7: 부품1.D2, R3.Pin_1
  N8: 부품1.D3_PWM, R4.Pin_1
  N9: 부품1.D4, LED1.A
  N10: 부품1.D5_PWM, LED1.APOS-A
  N11: 부품1.D6_PWM, LED1.E
  N12: 부품1.D7, LED1.D
  N13: LED1.DP, R4.Pin_0
  N14: LED1.F, R3.Pin_0
  N15: LED1.COL-C, R2.Pin_0
  N16: LED1.G, R1.Pin_0
